// Logisim project Boba Vending Machine.circ as structural Verilog: 5 circuits, main circuit main
module Money_Input (
  input  _1,
  input  in_2,
  input  _5,
  input  _10,
  input  _25,
  input  _50,
  input  _1_2,
  input  _5_2,
  input  _10_2,
  input  _20,
  output [11:0] out_11
);

  wire n12_bit_super_adder_1_out_11;
  wire [11:0] adder_1_out, n12_bit_super_adder_1_total, register_1_q;

  _12_bit_super_adder u_12_bit_super_adder_1 (
    .in_1({{11{1'b0}}, _1}), .in_2({{9{1'b0}}, _5, 1'b0, _5}), .in_3({{8{1'b0}}, _10, 1'b0, _10, 1'b0}),
    .in_4({{7{1'b0}}, {2{_25}}, 2'b00, _25}), .in_5({{6{1'b0}}, {2{_50}}, 2'b00, _50, 1'b0}),
    .in_6({{5{1'b0}}, {2{_1_2}}, 2'b00, _1_2, 2'b00}), .in_7({3'b000, {5{_5_2}}, 1'b0, _5_2, 2'b00}),
    .in_8({2'b00, {5{_10_2}}, 1'b0, _10_2, 3'b000}), .in_9({1'b0, {5{_20}}, 1'b0, _20, 4'b0000}),
    .Total(n12_bit_super_adder_1_total), .out_11(n12_bit_super_adder_1_out_11));
  Register #(.width(12)) register_1 (
    .D(n12_bit_super_adder_1_total), .en(n12_bit_super_adder_1_out_11), .Q(register_1_q),
    .clk(n12_bit_super_adder_1_out_11), .clr(in_2));
  Adder #(.width(12)) adder_1 (.a(register_1_q), .b(out_11), .out(adder_1_out));  // open: cin, cout
  Register #(.width(12)) register_2 (
    .D(adder_1_out), .en(n12_bit_super_adder_1_out_11), .Q(out_11), .clk(n12_bit_super_adder_1_out_11),
    .clr(in_2));
endmodule

module main (
  output [2:0] out_1
);

  wire button_1_out, button_2_out, button_3_out, button_4_out, button_5_out, button_6_out, button_7_out,
       button_8_out, button_9_out, button_10_out, button_11_out, button_12_out, Clr_out;
  wire [3:0] main_1_p2, main_1_p3, main_1_p4, main_1_p5;
  wire [11:0] money_input_1_out_11;

  LED Not_Enough_Money ();  // open: in
  LED led_1 ();  // open: in
  LED led_2 ();  // open: in
  LED led_3 ();  // open: in
  Button button_1 (.out(button_1_out));
  Button button_2 (.out(button_2_out));
  Button button_3 (.out(button_3_out));
  Button button_4 (.out(button_4_out));
  Button button_5 (.out(button_5_out));
  Button button_6 (.out(button_6_out));
  Button button_7 (.out(button_7_out));
  Button button_8 (.out(button_8_out));
  Button button_9 (.out(button_9_out));
  Button button_10 (.out(button_10_out));
  Button button_11 (.out(button_11_out));
  Button button_12 (.out(button_12_out));
  Button Buy ();  // open: out
  Money_Input money_input_1 (
    ._1(button_1_out), ._5(button_2_out), ._10(button_3_out), ._25(button_4_out), ._50(button_5_out),
    ._1_2(button_6_out), ._5_2(button_7_out), ._10_2(button_8_out), ._20(button_9_out), .in_2(Clr_out),
    .out_11(money_input_1_out_11));
  Flavor_Input flavor_input_1 (
    .in_1(button_10_out), .Flavor(out_1), .in_2(button_11_out), .in_3(button_12_out), .in_4(Clr_out));  // open: Price
  Button Clr (.out(Clr_out));
  Hex_Digit_Display hex_digit_display_1 (.value(main_1_p3));  // open: dp
  Hex_Digit_Display hex_digit_display_2 (.value(main_1_p2));  // open: dp
  Hex_Digit_Display hex_digit_display_3 (.value(main_1_p4));  // open: dp
  Hex_Digit_Display hex_digit_display_4 (.value(main_1_p5));  // open: dp
  // _12_Bit_BCD_Converter__Final___1__main main_1: pin names not known; wires that end beside it: money_input_1_out_11, main_1_p2, main_1_p3, main_1_p4, main_1_p5
  Hex_Digit_Display hex_digit_display_5 ();  // open: value, dp
  Hex_Digit_Display hex_digit_display_6 ();  // open: value, dp
  Hex_Digit_Display hex_digit_display_7 ();  // open: value, dp
  Hex_Digit_Display hex_digit_display_8 ();  // open: value, dp

  // Notes on the sheet:
  //   Money Input
  //   Flavor
  //   Total:
  //   Change:
endmodule

module Flavor_Input (
  input  in_1,
  input  in_2,
  input  in_3,
  input  in_4,
  output [11:0] Price,
  output [2:0] Flavor
);

  wire and_1_out, comparator_1_eq, comparator_2_eq, not_1_out, not_2_out;

  Comparator #(.width(3)) comparator_1 (.a({in_3, in_2, in_1}), .b(3'b000), .eq(comparator_1_eq));  // open: gt, lt
  not not_1 (not_1_out, comparator_1_eq);
  Register #(.width(3)) register_1 (.D({in_3, in_2, in_1}), .en(not_1_out), .Q(Flavor), .clk(not_1_out), .clr(in_4));
  Comparator #(.width(12)) comparator_2 (.a({12{1'b0}}), .b({12{1'b0}}), .eq(comparator_2_eq));  // open: gt, lt
  not not_2 (not_2_out, comparator_2_eq);
  and and_1 (and_1_out, Flavor[0], not_2_out);
endmodule

module Flavor_State (
  input  b,
  input  c,
  input  in_3,
  input  in_4,
  output out_5,
  output out_6,
  output out_7
);

  wire and_1_out, and_2_out, and_3_out, button_1_out, clock_1_out, not_1_out, not_2_out, not_3_out,
       not_4_out, not_5_out, not_6_out;

  Button button_1 (.out(button_1_out));
  not not_1 (not_1_out, b);
  not not_2 (not_2_out, c);
  not not_3 (not_3_out, button_1_out);
  not not_4 (not_4_out, c);
  not not_5 (not_5_out, button_1_out);
  not not_6 (not_6_out, b);
  and and_1 (and_1_out, button_1_out, not_1_out, not_2_out);
  and and_2 (and_2_out, not_3_out, b, not_4_out);
  and and_3 (and_3_out, not_5_out, not_6_out, c);
  Clock clock_1 (.out(clock_1_out));
  D_Flip_Flop d_ff_1 (.clk(clock_1_out), .D(and_1_out), .Q(out_5), .en(in_3), .reset(in_4));  // open: Qn, preset
  D_Flip_Flop d_ff_2 (.clk(clock_1_out), .D(and_2_out), .Q(out_6), .en(in_3), .reset(in_4));  // open: Qn, preset
  D_Flip_Flop d_ff_3 (.clk(clock_1_out), .D(and_3_out), .Q(out_7), .en(in_3), .reset(in_4));  // open: Qn, preset
endmodule

// Super adder
module _12_bit_super_adder (
  input  [11:0] in_1,
  input  [11:0] in_2,
  input  [11:0] in_3,
  input  [11:0] in_4,
  input  [11:0] in_5,
  input  [11:0] in_6,
  input  [11:0] in_7,
  input  [11:0] in_8,
  input  [11:0] in_9,
  output [11:0] Total,
  output out_11
);

  wire [11:0] adder_1_out, adder_2_out, adder_3_out, adder_4_out, adder_5_out, adder_6_out, adder_7_out;

  Adder #(.width(12)) adder_1 (.a(in_1), .b(in_2), .out(adder_1_out));  // open: cin, cout
  Adder #(.width(12)) adder_2 (.a(in_3), .b(in_4), .out(adder_2_out));  // open: cin, cout
  Adder #(.width(12)) adder_3 (.a(in_5), .b(in_6), .out(adder_3_out));  // open: cin, cout
  Adder #(.width(12)) adder_4 (.a(in_7), .b(in_8), .out(adder_4_out));  // open: cin, cout
  Adder #(.width(12)) adder_5 (.a(adder_1_out), .b(adder_2_out), .out(adder_5_out));  // open: cin, cout
  Adder #(.width(12)) adder_6 (.a(adder_3_out), .b(adder_4_out), .out(adder_6_out));  // open: cin, cout
  Adder #(.width(12)) adder_7 (.a(adder_5_out), .b(adder_6_out), .out(adder_7_out));  // open: cin, cout
  Adder #(.width(12)) adder_8 (.a(adder_7_out), .b(in_9), .out(Total));  // open: cin, cout
  Comparator #(.width(12)) comparator_1 (.a(Total), .b({12{1'b0}}), .gt(out_11));  // open: eq, lt
endmodule
